# Fritzing sketch SnailMailNotifier (saved by Fritzing 0.7.10b)

parts:
  D2F1 = D2F-FL Omron Snap Action Limit Switch with Level  # not connected
  Arduino_Ethernet_Shield1 = Arduino Ethernet Shield
  R1 = 10k Ω Resistor [package=THT]  # not connected
  LED2 = green LED - 5mm

nets:
  N1: Arduino_Ethernet_Shield1.GND, LED2.cathode
  N2: Arduino_Ethernet_Shield1.D9, LED2.anode

custom parts:
  D2F-FL Omron Snap Action Limit Switch with Level: Snap action switch with stainless steel lever.
